# Fritzing sketch scheme-grps-sim800-example (saved by Fritzing 0.9.3b)
breadboards: 1

parts:
  IC2 = SIM800L [package=THT]
  IC1 = Arduino Nano (Rev3.0)
  IC3 = DS18B20 1-Wire Temperature Sensor [part_number=DS18B20]
  R1 = Resistor [tolerance=±5% resistance=4.7k package=THT]
  IC4 = SPX29302 [package=q5-dd_spx29300]
  R2 = Resistor [tolerance=±5% resistance=47k package=THT]
  R3 = Resistor [tolerance=±5% resistance=22k package=THT]

nets:
  N1: IC2.5V, IC4.VOUT, R2.Pin_0
  N2: IC2.SIM_TXD, IC1.D9
  N3: IC2.SIM_RXD, IC1.D8
  GND: IC2.GND, IC1.GND, IC3.GND, IC4.GND, R3.Pin_1
  N4: IC1.D6, IC3.DQ, R1.Pin_0
  5V: IC1.5V, IC3.VDD, R1.Pin_1, IC4.ENABLE, IC4.VIN
  N5: IC4.ADJUST, R2.Pin_1

notes:
  +3.9v
